// Logisim project ç.circ as structural Verilog: 28 circuits, main circuit main
module main (
);

  Coder coder_1 ();  // open: CH0, CH1, CH2, CH3, CH4, CH5, CH6, CH7, CH8, CH9, A, B, C, D
endmodule

module Coder (
  input  CH0,
  input  CH1,
  input  CH2,
  input  CH3,
  input  CH4,
  input  CH5,
  input  CH6,
  input  CH7,
  input  CH8,
  input  CH9,
  output A,
  output B,
  output C,
  output D
);

  or or_1 (A, CH9, CH8);
  or or_2 (B, CH7, CH6, CH5, CH4);
  or or_3 (C, CH7, CH6, CH3, CH2);
  or or_4 (D, CH9, CH7, CH5, CH3, CH1);
endmodule

// a
module Segmento_a (
  input  A,
  input  B,
  input  C,
  input  D,
  output a_2
);

  wire not_1_out, not_2_out, or_1_out, or_2_out;

  not not_1 (not_1_out, B);
  not not_2 (not_2_out, D);
  or or_1 (or_1_out, A, not_1_out, C, D);
  or or_2 (or_2_out, A, B, C, not_2_out);
  and and_1 (a_2, or_2_out, or_1_out);
endmodule

// b
module segmento_b (
  input  A,
  input  B,
  input  C,
  input  D,
  output b_2
);

  wire not_1_out, not_2_out, not_3_out, or_1_out, or_2_out;

  not not_1 (not_1_out, B);
  not not_2 (not_2_out, C);
  not not_3 (not_3_out, D);
  or or_1 (or_1_out, A, not_1_out, C, not_3_out);
  or or_2 (or_2_out, A, not_1_out, not_2_out, D);
  and and_1 (b_2, or_1_out, or_2_out);
endmodule

// c
module seg_c (
  input  A,
  input  B,
  input  C,
  input  D,
  output c_2
);

  wire not_1_out;

  not not_1 (not_1_out, C);
  or or_1 (c_2, A, B, not_1_out, D);
endmodule

// d
module seg_d (
  input  A,
  input  B,
  input  C,
  input  D,
  output d_2
);

  wire not_1_out, not_2_out, not_3_out, not_4_out, not_5_out, or_1_out, or_2_out, or_3_out;

  or or_1 (or_1_out, A, B, C, not_1_out);
  not not_1 (not_1_out, D);
  not not_2 (not_2_out, B);
  or or_2 (or_2_out, A, not_2_out, C, D);
  not not_3 (not_3_out, B);
  or or_3 (or_3_out, A, not_3_out, not_4_out, not_5_out);
  not not_4 (not_4_out, C);
  not not_5 (not_5_out, D);
  and and_1 (d_2, or_1_out, or_2_out, or_3_out);
endmodule

// e
module seg_e (
  input  A,
  input  B,
  input  C,
  input  D,
  output e
);

  wire not_1_out, not_2_out, not_3_out, not_4_out, not_5_out, not_6_out, not_7_out, not_8_out, not_9_out,
       not_10_out, not_11_out, or_1_out, or_2_out, or_3_out, or_4_out, or_5_out, or_6_out;

  not not_1 (not_1_out, D);
  not not_2 (not_2_out, C);
  not not_3 (not_3_out, D);
  not not_4 (not_4_out, B);
  not not_5 (not_5_out, B);
  not not_6 (not_6_out, D);
  not not_7 (not_7_out, B);
  not not_8 (not_8_out, C);
  not not_9 (not_9_out, D);
  not not_10 (not_10_out, A);
  not not_11 (not_11_out, D);
  or or_1 (or_1_out, A, B, C, not_1_out);
  or or_2 (or_2_out, A, B, not_2_out, not_3_out);
  or or_3 (or_3_out, A, not_4_out, C, D);
  or or_4 (or_4_out, A, not_5_out, C, not_6_out);
  or or_5 (or_5_out, A, not_7_out, not_8_out, not_9_out);
  or or_6 (or_6_out, not_10_out, B, C, not_11_out);
  and and_1 (e, or_1_out, or_2_out, or_3_out, or_4_out, or_5_out, or_6_out);
endmodule

// f
module seg_f (
  input  A,
  input  B,
  input  C,
  input  D,
  output f
);

  wire not_1_out, not_2_out, not_3_out, not_4_out, not_5_out, not_6_out, not_7_out, or_1_out, or_2_out,
       or_3_out, or_4_out;

  or or_1 (or_1_out, A, B, C, not_1_out);
  not not_1 (not_1_out, D);
  or or_2 (or_2_out, A, B, not_2_out, D);
  not not_2 (not_2_out, C);
  or or_3 (or_3_out, A, B, not_3_out, not_4_out);
  not not_3 (not_3_out, C);
  not not_4 (not_4_out, D);
  not not_5 (not_5_out, B);
  or or_4 (or_4_out, A, not_5_out, not_6_out, not_7_out);
  not not_6 (not_6_out, C);
  not not_7 (not_7_out, D);
  and and_1 (f, or_1_out, or_2_out, or_3_out, or_4_out);
endmodule

// g
module seg_g (
  input  A,
  input  B,
  input  C,
  input  D,
  output g
);

  wire not_1_out, not_2_out, not_3_out, not_4_out, or_1_out, or_2_out, or_3_out;

  not not_1 (not_1_out, D);
  not not_2 (not_2_out, B);
  not not_3 (not_3_out, C);
  not not_4 (not_4_out, D);
  or or_1 (or_1_out, A, B, C, D);
  or or_2 (or_2_out, A, B, C, not_1_out);
  or or_3 (or_3_out, A, not_2_out, not_3_out, not_4_out);
  and and_1 (g, or_1_out, or_2_out, or_3_out);
endmodule

module Decoder (
  input  A,
  input  B,
  input  C,
  input  D,
  output a_2,
  output b_2,
  output c_2,
  output d_2,
  output e,
  output f,
  output g
);

  Segmento_a segmento_a_1 (.A(A), .B(B), .C(C), .D(D), .a_2(a_2));
  segmento_b segmento_b_1 (.A(A), .B(B), .C(C), .D(D), .b_2(b_2));
  seg_c seg_c_1 (.A(A), .B(B), .C(C), .D(D), .c_2(c_2));
  seg_d seg_d_1 (.A(A), .B(B), .C(C), .D(D), .d_2(d_2));
  seg_e seg_e_1 (.A(A), .B(B), .C(C), .D(D), .e(e));
  seg_f seg_f_1 (.A(A), .B(B), .C(C), .D(D), .f(f));
  seg_g seg_g_1 (.A(A), .B(B), .C(C), .D(D), .g(g));
endmodule

module uniao (
  input  _0,
  input  _1,
  input  _2,
  input  _3,
  input  _4,
  input  _5,
  input  _6,
  input  _7,
  input  _8,
  input  _9
);

  wire coder_1_a, coder_1_b, coder_1_c, coder_1_d, decoder_1_a_2, decoder_1_b_2, decoder_1_c_2,
       decoder_1_d_2, decoder_1_e, decoder_1_f, decoder_1_g;

  Coder coder_1 (
    .CH0(_0), .CH1(_1), .CH2(_2), .CH3(_3), .CH4(_4), .CH5(_5), .CH6(_6), .CH7(_7), .CH8(_8), .CH9(_9),
    .A(coder_1_a), .B(coder_1_b), .C(coder_1_c), .D(coder_1_d));
  Decoder decoder_1 (
    .A(coder_1_a), .B(coder_1_b), .C(coder_1_c), .D(coder_1_d), .a_2(decoder_1_a_2), .b_2(decoder_1_b_2),
    .c_2(decoder_1_c_2), .d_2(decoder_1_d_2), .e(decoder_1_e), .f(decoder_1_f), .g(decoder_1_g));
  _7_Segment_Display u_7_segment_display_1 (
    .g(decoder_1_g), .f(decoder_1_f), .a(decoder_1_a_2), .b(decoder_1_b_2), .e(decoder_1_e),
    .d(decoder_1_d_2), .c(decoder_1_c_2));  // open: dp
endmodule

module MUX (
  input  A,
  input  i0,
  input  i1,
  output out_4
);

  wire and_1_out, and_2_out, not_1_out;

  not not_1 (not_1_out, A);
  and and_1 (and_1_out, not_1_out, i0);
  and and_2 (and_2_out, A, i1);
  or or_1 (out_4, and_1_out, and_2_out);
endmodule

module Mux_4_canais (
  input  i0,
  input  i1,
  input  i2,
  input  i3,
  input  A,
  input  B,
  output out_7
);

  wire and_1_out, and_2_out, and_3_out, and_4_out, not_1_out, not_2_out, not_3_out, not_4_out;

  not not_1 (not_1_out, A);
  not not_2 (not_2_out, B);
  not not_3 (not_3_out, A);
  not not_4 (not_4_out, B);
  and and_1 (and_1_out, not_1_out, not_2_out, i0);
  and and_2 (and_2_out, not_3_out, B, i1);
  and and_3 (and_3_out, A, not_4_out, i2);
  and and_4 (and_4_out, A, B, i3);
  or or_1 (out_7, and_1_out, and_2_out, and_3_out, and_4_out);
endmodule

module demux_de_2_canais (
  input  A,
  input  i0,
  output s0,
  output s1
);

  wire not_1_out;

  not not_1 (not_1_out, A);
  and and_1 (s0, not_1_out, i0);
  and and_2 (s1, A, i0);
endmodule

module demux_4_canais (
  input  B,
  input  A,
  input  i0,
  output s0,
  output s01,
  output s02,
  output s03
);

  wire not_1_out, not_2_out, not_3_out, not_4_out;

  not not_1 (not_1_out, A);
  not not_2 (not_2_out, B);
  not not_3 (not_3_out, A);
  not not_4 (not_4_out, B);
  and and_1 (s0, not_1_out, not_2_out, i0);
  and and_2 (s01, not_3_out, B, i0);
  and and_3 (s02, A, not_4_out, i0);
  and and_4 (s03, A, B, i0);
endmodule

// HA
module half_adder (
  input  A,
  input  B,
  output S,
  output T
);

  xor xor_1 (S, A, B);
  and and_1 (T, A, B);
endmodule

// FA
module full_adder (
  input  A,
  input  B,
  input  Te,
  output S,
  output T
);

  wire and_1_out, and_2_out, and_3_out, and_4_out, and_5_out, and_6_out, and_7_out, not_1_out, not_2_out,
       not_3_out, not_4_out, not_5_out, not_6_out;

  not not_1 (not_1_out, B);
  not not_2 (not_2_out, Te);
  not not_3 (not_3_out, A);
  not not_4 (not_4_out, B);
  not not_5 (not_5_out, A);
  not not_6 (not_6_out, Te);
  and and_1 (and_1_out, A, not_1_out, not_2_out);
  and and_2 (and_2_out, not_3_out, not_4_out, Te);
  and and_3 (and_3_out, A, B, Te);
  and and_4 (and_4_out, not_5_out, B, not_6_out);
  and and_5 (and_5_out, A, Te);
  and and_6 (and_6_out, A, B);
  and and_7 (and_7_out, B, Te);
  or or_1 (S, and_1_out, and_2_out, and_3_out, and_4_out);
  or or_2 (T, and_5_out, and_6_out, and_7_out);
endmodule

module Somador_de_2_bits (
  input  A1,
  input  A0,
  input  B1,
  input  B0,
  output s2,
  output s1,
  output s0
);

  wire half_adder_1_t;

  full_adder full_adder_1 (.A(A1), .B(B1), .Te(half_adder_1_t), .S(s1), .T(s2));
  half_adder half_adder_1 (.A(B0), .B(A0), .S(s0), .T(half_adder_1_t));
endmodule

module somador_de_4_bits (
  input  B3,
  input  A3,
  input  B2,
  input  A2,
  input  B1,
  input  A1,
  input  B0,
  input  A0,
  output s2,
  output s1,
  output s0,
  output s4,
  output s3
);

  wire full_adder_2_t, full_adder_3_t, half_adder_1_t;

  full_adder full_adder_1 (.A(B3), .B(A3), .Te(full_adder_2_t), .S(s3), .T(s4));
  full_adder full_adder_2 (.A(B2), .B(A2), .Te(full_adder_3_t), .S(s2), .T(full_adder_2_t));
  full_adder full_adder_3 (.A(B1), .B(A1), .Te(half_adder_1_t), .S(s1), .T(full_adder_3_t));
  half_adder half_adder_1 (.A(B0), .B(A0), .S(s0), .T(half_adder_1_t));
endmodule

module subtrator_de_4_bits (
  input  A3,
  input  A2,
  input  A1,
  input  A0,
  input  in_5,
  input  in_6,
  input  in_7,
  input  in_8,
  input  B3,
  input  B2,
  input  B1,
  input  B0,
  output out_13,
  output out_14,
  output out_15,
  output out_16,
  output out_17,
  output out_18
);

  wire not_1_out, not_2_out, not_3_out, not_4_out, somador_de_4_bits_1_s0, somador_de_4_bits_1_s1,
       somador_de_4_bits_1_s2, somador_de_4_bits_1_s3;

  not not_1 (not_1_out, B3);
  not not_2 (not_2_out, B2);
  not not_3 (not_3_out, B1);
  not not_4 (not_4_out, B0);
  somador_de_4_bits somador_de_4_bits_1 (
    .B3(not_1_out), .A3(A3), .B2(not_2_out), .A2(A2), .B1(not_3_out), .A1(A1), .B0(not_4_out), .A0(A0),
    .s4(out_13), .s3(somador_de_4_bits_1_s3), .s2(somador_de_4_bits_1_s2), .s1(somador_de_4_bits_1_s1),
    .s0(somador_de_4_bits_1_s0));
  somador_de_4_bits somador_de_4_bits_2 (
    .B3(somador_de_4_bits_1_s3), .A3(in_5), .B2(somador_de_4_bits_1_s2), .A2(in_6),
    .B1(somador_de_4_bits_1_s1), .A1(in_7), .B0(somador_de_4_bits_1_s0), .A0(in_8), .s4(out_14), .s3(out_15),
    .s2(out_16), .s1(out_17), .s0(out_18));
endmodule

module Calculadora (
  input  _5,
  input  _4,
  input  _6,
  input  _3,
  input  _7,
  input  _2,
  input  _1,
  input  _8,
  input  _0,
  input  _9,
  input  _5_2,
  input  _4_2,
  input  _6_2,
  input  _3_2,
  input  _7_2,
  input  _2_2,
  input  _1_2,
  input  _8_2,
  input  _0_2,
  input  _9_2,
  input  in_21,
  input  in_22,
  input  in_23,
  input  escolha_mux,
  output out_25,
  output out_26,
  output out_27
);

  wire coder_1_a, coder_1_b, coder_1_c, coder_1_d, coder_2_a, coder_2_b, coder_2_c, coder_2_d, decoder_1_a_2,
       decoder_1_b_2, decoder_1_c_2, decoder_1_d_2, decoder_1_e, decoder_1_f, decoder_1_g, mux_1_out_4,
       mux_2_out_4, mux_3_out_4, mux_4_out_4, not_1_out, not_2_out, not_3_out, not_4_out,
       somador_de_4_bits_1_s0, somador_de_4_bits_1_s1, somador_de_4_bits_1_s2, somador_de_4_bits_1_s3,
       somador_de_4_bits_2_s0, somador_de_4_bits_2_s1, somador_de_4_bits_2_s2, somador_de_4_bits_2_s3,
       somador_de_4_bits_3_s0, somador_de_4_bits_3_s1, somador_de_4_bits_3_s2, somador_de_4_bits_3_s3;

  Coder coder_1 (
    .CH0(_0), .CH1(_1), .CH2(_2), .CH3(_3), .CH4(_4), .CH5(_5), .CH6(_6), .CH7(_7), .CH8(_8), .CH9(_9),
    .A(coder_1_a), .B(coder_1_b), .C(coder_1_c), .D(coder_1_d));
  Coder coder_2 (
    .CH0(_0_2), .CH1(_1_2), .CH2(_2_2), .CH3(_3_2), .CH4(_4_2), .CH5(_5_2), .CH6(_6_2), .CH7(_7_2),
    .CH8(_8_2), .CH9(_9_2), .A(coder_2_a), .B(coder_2_b), .C(coder_2_c), .D(coder_2_d));
  not not_1 (not_1_out, coder_2_a);
  not not_2 (not_2_out, coder_2_b);
  not not_3 (not_3_out, coder_2_c);
  not not_4 (not_4_out, coder_2_d);
  somador_de_4_bits somador_de_4_bits_1 (
    .B3(not_1_out), .A3(in_21), .B2(not_2_out), .A2(in_22), .B1(not_3_out), .A1(in_23), .B0(not_4_out),
    .A0(1'b1), .s4(out_26), .s3(somador_de_4_bits_1_s3), .s2(somador_de_4_bits_1_s2),
    .s1(somador_de_4_bits_1_s1), .s0(somador_de_4_bits_1_s0));
  somador_de_4_bits somador_de_4_bits_2 (
    .B3(coder_2_a), .A3(coder_1_a), .B2(coder_2_b), .A2(coder_1_b), .B1(coder_2_c), .A1(coder_1_c),
    .B0(coder_2_d), .A0(coder_1_d), .s4(out_25), .s3(somador_de_4_bits_2_s3), .s2(somador_de_4_bits_2_s2),
    .s1(somador_de_4_bits_2_s1), .s0(somador_de_4_bits_2_s0));
  somador_de_4_bits somador_de_4_bits_3 (
    .B3(somador_de_4_bits_1_s3), .A3(coder_1_a), .B2(somador_de_4_bits_1_s2), .A2(coder_1_b),
    .B1(somador_de_4_bits_1_s1), .A1(coder_1_c), .B0(somador_de_4_bits_1_s0), .A0(coder_1_d), .s4(out_27),
    .s3(somador_de_4_bits_3_s3), .s2(somador_de_4_bits_3_s2), .s1(somador_de_4_bits_3_s1),
    .s0(somador_de_4_bits_3_s0));
  MUX mux_1 (.A(escolha_mux), .i0(somador_de_4_bits_2_s3), .i1(somador_de_4_bits_3_s3), .out_4(mux_1_out_4));
  MUX mux_2 (.A(escolha_mux), .i0(somador_de_4_bits_2_s2), .i1(somador_de_4_bits_3_s2), .out_4(mux_2_out_4));
  MUX mux_3 (.A(escolha_mux), .i0(somador_de_4_bits_2_s1), .i1(somador_de_4_bits_3_s1), .out_4(mux_3_out_4));
  MUX mux_4 (.A(escolha_mux), .i0(somador_de_4_bits_2_s0), .i1(somador_de_4_bits_3_s0), .out_4(mux_4_out_4));
  Decoder decoder_1 (
    .A(mux_1_out_4), .B(mux_2_out_4), .C(mux_3_out_4), .D(mux_4_out_4), .a_2(decoder_1_a_2),
    .b_2(decoder_1_b_2), .c_2(decoder_1_c_2), .d_2(decoder_1_d_2), .e(decoder_1_e), .f(decoder_1_f),
    .g(decoder_1_g));
  _7_Segment_Display u_7_segment_display_1 (
    .g(decoder_1_g), .f(decoder_1_f), .a(decoder_1_a_2), .b(decoder_1_b_2), .e(decoder_1_e),
    .d(decoder_1_d_2), .c(decoder_1_c_2));  // open: dp

  // Notes on the sheet:
  //   Coder A
  //   Coder B
  //   somador +1
  //   somador
  //   somador para subtrador
  //   mux 2 canais
  //   decoder
endmodule

module contador (
  input  in_1
);

  wire clock_1_out, decoder_1_a_2, decoder_1_b_2, decoder_1_c_2, decoder_1_d_2, decoder_1_e, decoder_1_f,
       decoder_1_g, t_ff_1_q, t_ff_2_q, t_ff_3_q;

  Clock clock_1 (.out(clock_1_out));
  T_Flip_Flop #(.trigger("falling")) t_ff_1 (.clk(clock_1_out), .T(1'b1), .Q(t_ff_1_q));  // open: Qn, preset, reset, en
  T_Flip_Flop #(.trigger("falling")) t_ff_2 (.clk(t_ff_1_q), .T(1'b1), .Q(t_ff_2_q));  // open: Qn, preset, reset, en
  T_Flip_Flop #(.trigger("falling")) t_ff_3 (.clk(t_ff_2_q), .T(1'b1), .Q(t_ff_3_q));  // open: Qn, preset, reset, en
  Decoder decoder_1 (
    .A(in_1), .B(t_ff_3_q), .C(t_ff_2_q), .D(t_ff_1_q), .a_2(decoder_1_a_2), .b_2(decoder_1_b_2),
    .c_2(decoder_1_c_2), .d_2(decoder_1_d_2), .e(decoder_1_e), .f(decoder_1_f), .g(decoder_1_g));
  _7_Segment_Display u_7_segment_display_1 (
    .g(decoder_1_g), .f(decoder_1_f), .a(decoder_1_a_2), .b(decoder_1_b_2), .e(decoder_1_e),
    .d(decoder_1_d_2), .c(decoder_1_c_2));  // open: dp
endmodule

module \contador_assíncrono_n8_crescente_decrescente  (
  input  in_1,
  input  seletor
);

  wire clock_1_out, decoder_1_a_2, decoder_1_b_2, decoder_1_c_2, decoder_1_d_2, decoder_1_e, decoder_1_f,
       decoder_1_g, mux_1_out_4, mux_2_out_4, mux_3_out_4, t_ff_1_q, t_ff_1_qn, t_ff_2_q, t_ff_2_qn,
       t_ff_3_q, t_ff_3_qn;

  Clock clock_1 (.out(clock_1_out));
  T_Flip_Flop #(.trigger("falling")) t_ff_1 (
    .clk(clock_1_out), .T(1'b1), .Q(t_ff_1_q), .Qn(t_ff_1_qn));  // open: preset, reset, en
  T_Flip_Flop #(.trigger("falling")) t_ff_2 (
    .clk(t_ff_1_q), .T(1'b1), .Q(t_ff_2_q), .Qn(t_ff_2_qn));  // open: preset, reset, en
  MUX mux_1 (.A(seletor), .i0(t_ff_1_q), .i1(t_ff_1_qn), .out_4(mux_1_out_4));
  MUX mux_2 (.A(seletor), .i0(t_ff_2_q), .i1(t_ff_2_qn), .out_4(mux_2_out_4));
  T_Flip_Flop #(.trigger("falling")) t_ff_3 (
    .clk(t_ff_2_q), .T(1'b1), .Q(t_ff_3_q), .Qn(t_ff_3_qn));  // open: preset, reset, en
  MUX mux_3 (.A(seletor), .i0(t_ff_3_q), .i1(t_ff_3_qn), .out_4(mux_3_out_4));
  Decoder decoder_1 (
    .A(in_1), .B(mux_3_out_4), .C(mux_2_out_4), .D(mux_1_out_4), .a_2(decoder_1_a_2), .b_2(decoder_1_b_2),
    .c_2(decoder_1_c_2), .d_2(decoder_1_d_2), .e(decoder_1_e), .f(decoder_1_f), .g(decoder_1_g));
  _7_Segment_Display u_7_segment_display_1 (
    .g(decoder_1_g), .f(decoder_1_f), .a(decoder_1_a_2), .b(decoder_1_b_2), .e(decoder_1_e),
    .d(decoder_1_d_2), .c(decoder_1_c_2));  // open: dp
endmodule

module \contador_síncrono_crescente_n4  (
  input  in_1
);

  wire and_1_out, clock_1_out, decoder_1_a_2, decoder_1_b_2, decoder_1_c_2, decoder_1_d_2, decoder_1_e,
       decoder_1_f, decoder_1_g, t_ff_1_q, t_ff_2_q, t_ff_3_q;

  Clock clock_1 (.out(clock_1_out));
  T_Flip_Flop #(.trigger("falling")) t_ff_1 (.clk(clock_1_out), .T(1'b1), .Q(t_ff_1_q));  // open: Qn, preset, reset, en
  T_Flip_Flop #(.trigger("falling")) t_ff_2 (
    .clk(clock_1_out), .T(t_ff_1_q), .Q(t_ff_2_q));  // open: Qn, preset, reset, en
  and and_1 (and_1_out, t_ff_1_q, t_ff_2_q);
  T_Flip_Flop #(.trigger("falling")) t_ff_3 (
    .clk(clock_1_out), .T(and_1_out), .Q(t_ff_3_q));  // open: Qn, preset, reset, en
  Decoder decoder_1 (
    .A(in_1), .B(t_ff_3_q), .C(t_ff_2_q), .D(t_ff_1_q), .a_2(decoder_1_a_2), .b_2(decoder_1_b_2),
    .c_2(decoder_1_c_2), .d_2(decoder_1_d_2), .e(decoder_1_e), .f(decoder_1_f), .g(decoder_1_g));
  _7_Segment_Display u_7_segment_display_1 (
    .g(decoder_1_g), .f(decoder_1_f), .a(decoder_1_a_2), .b(decoder_1_b_2), .e(decoder_1_e),
    .d(decoder_1_d_2), .c(decoder_1_c_2));  // open: dp
endmodule

module contador_assincrono_m16 (
  input  CLK,
  input  CLEAR,
  output C,
  output B,
  output A,
  output D
);

  T_Flip_Flop #(.trigger("falling")) t_ff_1 (.clk(CLK), .T(1'b1), .Q(D), .reset(CLEAR));  // open: Qn, preset, en
  T_Flip_Flop #(.trigger("falling")) t_ff_2 (.clk(D), .T(1'b1), .Q(C), .reset(CLEAR));  // open: Qn, preset, en
  T_Flip_Flop #(.trigger("falling")) t_ff_3 (.clk(C), .T(1'b1), .Q(B), .reset(CLEAR));  // open: Qn, preset, en
  T_Flip_Flop #(.trigger("falling")) t_ff_4 (.clk(B), .T(1'b1), .Q(A), .reset(CLEAR));  // open: Qn, preset, en
endmodule

module contador_crescente_assincrono_de_0_a_9 (
);

  wire and_1_out, and_2_out, clock_1_out, contador_assincrono_m16_1_a, contador_assincrono_m16_1_b,
       contador_assincrono_m16_1_c, contador_assincrono_m16_1_d, contador_assincrono_m16_2_a,
       contador_assincrono_m16_2_b, contador_assincrono_m16_2_c, contador_assincrono_m16_2_d, decoder_1_a_2,
       decoder_1_b_2, decoder_1_c_2, decoder_1_d_2, decoder_1_e, decoder_1_f, decoder_1_g, decoder_2_a_2,
       decoder_2_b_2, decoder_2_c_2, decoder_2_d_2, decoder_2_e, decoder_2_f, decoder_2_g;

  and and_1 (and_1_out, contador_assincrono_m16_1_c, contador_assincrono_m16_1_b);
  and and_2 (and_2_out, contador_assincrono_m16_2_c, contador_assincrono_m16_2_a);
  contador_assincrono_m16 contador_assincrono_m16_1 (
    .CLK(and_2_out), .CLEAR(and_1_out), .D(contador_assincrono_m16_1_d), .C(contador_assincrono_m16_1_c),
    .B(contador_assincrono_m16_1_b), .A(contador_assincrono_m16_1_a));
  Clock clock_1 (.out(clock_1_out));
  contador_assincrono_m16 contador_assincrono_m16_2 (
    .CLK(clock_1_out), .CLEAR(and_2_out), .D(contador_assincrono_m16_2_d), .C(contador_assincrono_m16_2_c),
    .B(contador_assincrono_m16_2_b), .A(contador_assincrono_m16_2_a));
  Decoder decoder_1 (
    .A(contador_assincrono_m16_1_a), .B(contador_assincrono_m16_1_b), .C(contador_assincrono_m16_1_c),
    .D(contador_assincrono_m16_1_d), .a_2(decoder_1_a_2), .b_2(decoder_1_b_2), .c_2(decoder_1_c_2),
    .d_2(decoder_1_d_2), .e(decoder_1_e), .f(decoder_1_f), .g(decoder_1_g));
  Decoder decoder_2 (
    .A(contador_assincrono_m16_2_a), .B(contador_assincrono_m16_2_b), .C(contador_assincrono_m16_2_c),
    .D(contador_assincrono_m16_2_d), .a_2(decoder_2_a_2), .b_2(decoder_2_b_2), .c_2(decoder_2_c_2),
    .d_2(decoder_2_d_2), .e(decoder_2_e), .f(decoder_2_f), .g(decoder_2_g));
  _7_Segment_Display u_7_segment_display_1 (
    .g(decoder_1_g), .f(decoder_1_f), .a(decoder_1_a_2), .b(decoder_1_b_2), .e(decoder_1_e),
    .d(decoder_1_d_2), .c(decoder_1_c_2));  // open: dp
  _7_Segment_Display u_7_segment_display_2 (
    .g(decoder_2_g), .f(decoder_2_f), .a(decoder_2_a_2), .b(decoder_2_b_2), .e(decoder_2_e),
    .d(decoder_2_d_2), .c(decoder_2_c_2));  // open: dp
endmodule

module \Relógio_Digital  (
  input  in_1
);

  wire and_1_out, and_2_out, and_3_out, and_4_out, and_5_out, and_6_out, clock_1_out,
       contador_assincrono_m16_1_a, contador_assincrono_m16_1_b, contador_assincrono_m16_1_c,
       contador_assincrono_m16_1_d, contador_assincrono_m16_2_a, contador_assincrono_m16_2_b,
       contador_assincrono_m16_2_c, contador_assincrono_m16_2_d, contador_assincrono_m16_3_a,
       contador_assincrono_m16_3_b, contador_assincrono_m16_3_c, contador_assincrono_m16_3_d,
       contador_assincrono_m16_4_a, contador_assincrono_m16_4_b, contador_assincrono_m16_4_c,
       contador_assincrono_m16_4_d, contador_assincrono_m16_5_a, contador_assincrono_m16_5_b,
       contador_assincrono_m16_5_c, contador_assincrono_m16_5_d, contador_assincrono_m16_6_a,
       contador_assincrono_m16_6_b, contador_assincrono_m16_6_c, contador_assincrono_m16_6_d, decoder_1_a_2,
       decoder_1_b_2, decoder_1_c_2, decoder_1_d_2, decoder_1_e, decoder_1_f, decoder_1_g, decoder_2_a_2,
       decoder_2_b_2, decoder_2_c_2, decoder_2_d_2, decoder_2_e, decoder_2_f, decoder_2_g, decoder_3_a_2,
       decoder_3_b_2, decoder_3_c_2, decoder_3_d_2, decoder_3_e, decoder_3_f, decoder_3_g, decoder_4_a_2,
       decoder_4_b_2, decoder_4_c_2, decoder_4_d_2, decoder_4_e, decoder_4_f, decoder_4_g, decoder_5_a_2,
       decoder_5_b_2, decoder_5_c_2, decoder_5_d_2, decoder_5_e, decoder_5_f, decoder_5_g, decoder_6_a_2,
       decoder_6_b_2, decoder_6_c_2, decoder_6_d_2, decoder_6_e, decoder_6_f, decoder_6_g, or_1_out,
       or_2_out, or_3_out, or_4_out, or_5_out, or_6_out;

  and and_1 (and_1_out, contador_assincrono_m16_1_c, contador_assincrono_m16_1_d);
  or or_1 (or_1_out, in_1, and_1_out);
  contador_assincrono_m16 contador_assincrono_m16_1 (
    .CLK(and_2_out), .CLEAR(or_1_out), .D(contador_assincrono_m16_1_d), .C(contador_assincrono_m16_1_c),
    .B(contador_assincrono_m16_1_b), .A(contador_assincrono_m16_1_a));
  and and_2 (and_2_out, contador_assincrono_m16_2_c, contador_assincrono_m16_2_a);
  Decoder decoder_1 (
    .A(contador_assincrono_m16_1_a), .B(contador_assincrono_m16_1_b), .C(contador_assincrono_m16_1_c),
    .D(contador_assincrono_m16_1_d), .a_2(decoder_1_a_2), .b_2(decoder_1_b_2), .c_2(decoder_1_c_2),
    .d_2(decoder_1_d_2), .e(decoder_1_e), .f(decoder_1_f), .g(decoder_1_g));
  or or_2 (or_2_out, in_1, and_2_out);
  contador_assincrono_m16 contador_assincrono_m16_2 (
    .CLK(and_3_out), .CLEAR(or_2_out), .D(contador_assincrono_m16_2_d), .C(contador_assincrono_m16_2_c),
    .B(contador_assincrono_m16_2_b), .A(contador_assincrono_m16_2_a));
  and and_3 (and_3_out, contador_assincrono_m16_3_b, contador_assincrono_m16_3_c);
  Decoder decoder_2 (
    .A(contador_assincrono_m16_2_a), .B(contador_assincrono_m16_2_b), .C(contador_assincrono_m16_2_c),
    .D(contador_assincrono_m16_2_d), .a_2(decoder_2_a_2), .b_2(decoder_2_b_2), .c_2(decoder_2_c_2),
    .d_2(decoder_2_d_2), .e(decoder_2_e), .f(decoder_2_f), .g(decoder_2_g));
  or or_3 (or_3_out, in_1, and_3_out);
  contador_assincrono_m16 contador_assincrono_m16_3 (
    .CLK(and_4_out), .CLEAR(or_3_out), .D(contador_assincrono_m16_3_d), .C(contador_assincrono_m16_3_c),
    .B(contador_assincrono_m16_3_b), .A(contador_assincrono_m16_3_a));
  _7_Segment_Display u_7_segment_display_1 (
    .g(decoder_1_g), .f(decoder_1_f), .a(decoder_1_c_2), .b(decoder_1_a_2), .e(decoder_1_e),
    .d(decoder_1_d_2), .c(decoder_1_b_2));  // open: dp
  and and_4 (and_4_out, contador_assincrono_m16_4_a, contador_assincrono_m16_4_c);
  Decoder decoder_3 (
    .A(contador_assincrono_m16_3_a), .B(contador_assincrono_m16_3_b), .C(contador_assincrono_m16_3_c),
    .D(contador_assincrono_m16_3_d), .a_2(decoder_3_a_2), .b_2(decoder_3_b_2), .c_2(decoder_3_c_2),
    .d_2(decoder_3_d_2), .e(decoder_3_e), .f(decoder_3_f), .g(decoder_3_g));
  or or_4 (or_4_out, in_1, and_4_out);
  contador_assincrono_m16 contador_assincrono_m16_4 (
    .CLK(and_5_out), .CLEAR(or_4_out), .D(contador_assincrono_m16_4_d), .C(contador_assincrono_m16_4_c),
    .B(contador_assincrono_m16_4_b), .A(contador_assincrono_m16_4_a));
  and and_5 (and_5_out, contador_assincrono_m16_5_b, contador_assincrono_m16_5_c);
  Decoder decoder_4 (
    .A(contador_assincrono_m16_4_a), .B(contador_assincrono_m16_4_b), .C(contador_assincrono_m16_4_c),
    .D(contador_assincrono_m16_4_d), .a_2(decoder_4_a_2), .b_2(decoder_4_b_2), .c_2(decoder_4_c_2),
    .d_2(decoder_4_d_2), .e(decoder_4_e), .f(decoder_4_f), .g(decoder_4_g));
  or or_5 (or_5_out, in_1, and_5_out, and_5_out);
  contador_assincrono_m16 contador_assincrono_m16_5 (
    .CLK(and_6_out), .CLEAR(or_5_out), .D(contador_assincrono_m16_5_d), .C(contador_assincrono_m16_5_c),
    .B(contador_assincrono_m16_5_b), .A(contador_assincrono_m16_5_a));
  _7_Segment_Display u_7_segment_display_2 (
    .g(decoder_2_g), .f(decoder_2_f), .a(decoder_2_b_2), .b(decoder_2_c_2), .e(decoder_2_e),
    .d(decoder_2_a_2), .c(decoder_2_d_2));  // open: dp
  _7_Segment_Display u_7_segment_display_3 (
    .g(decoder_3_g), .f(decoder_3_f), .a(decoder_3_a_2), .b(decoder_3_b_2), .e(decoder_3_e),
    .d(decoder_3_d_2), .c(decoder_3_c_2));  // open: dp
  LED led_1 ();  // open: in
  LED led_2 ();  // open: in
  and and_6 (and_6_out, contador_assincrono_m16_6_a, contador_assincrono_m16_6_c);
  or or_6 (or_6_out, in_1, and_6_out);
  contador_assincrono_m16 contador_assincrono_m16_6 (
    .CLK(clock_1_out), .CLEAR(or_6_out), .D(contador_assincrono_m16_6_d), .C(contador_assincrono_m16_6_c),
    .B(contador_assincrono_m16_6_b), .A(contador_assincrono_m16_6_a));
  Decoder decoder_5 (
    .A(contador_assincrono_m16_5_a), .B(contador_assincrono_m16_5_b), .C(contador_assincrono_m16_5_c),
    .D(contador_assincrono_m16_5_d), .a_2(decoder_5_a_2), .b_2(decoder_5_b_2), .c_2(decoder_5_c_2),
    .d_2(decoder_5_d_2), .e(decoder_5_e), .f(decoder_5_f), .g(decoder_5_g));
  _7_Segment_Display u_7_segment_display_4 (
    .g(decoder_4_g), .f(decoder_4_f), .a(decoder_4_a_2), .b(decoder_4_b_2), .e(decoder_4_e),
    .d(decoder_4_d_2), .c(decoder_4_c_2));  // open: dp
  LED led_3 ();  // open: in
  LED led_4 ();  // open: in
  Decoder decoder_6 (
    .A(contador_assincrono_m16_6_a), .B(contador_assincrono_m16_6_b), .C(contador_assincrono_m16_6_c),
    .D(contador_assincrono_m16_6_d), .a_2(decoder_6_a_2), .b_2(decoder_6_b_2), .c_2(decoder_6_c_2),
    .d_2(decoder_6_d_2), .e(decoder_6_e), .f(decoder_6_f), .g(decoder_6_g));
  _7_Segment_Display u_7_segment_display_5 (
    .g(decoder_5_g), .f(decoder_5_f), .a(decoder_5_a_2), .b(decoder_5_b_2), .e(decoder_5_e),
    .d(decoder_5_d_2), .c(decoder_5_c_2));  // open: dp
  _7_Segment_Display u_7_segment_display_6 (
    .g(decoder_6_g), .f(decoder_6_f), .a(decoder_6_a_2), .b(decoder_6_b_2), .e(decoder_6_e),
    .d(decoder_6_d_2), .c(decoder_6_c_2));  // open: dp
  Clock clock_1 (.out(clock_1_out));
endmodule

module \Relógio_Digital_2  (
  input  RESET
);

  wire and_1_out, and_2_out, and_3_out, and_4_out, and_5_out, and_6_out, and_7_out, clock_1_out,
       contador_assincrono_m16_1_a, contador_assincrono_m16_1_b, contador_assincrono_m16_1_c,
       contador_assincrono_m16_1_d, contador_assincrono_m16_2_a, contador_assincrono_m16_2_b,
       contador_assincrono_m16_2_c, contador_assincrono_m16_2_d, contador_assincrono_m16_3_a,
       contador_assincrono_m16_3_b, contador_assincrono_m16_3_c, contador_assincrono_m16_3_d,
       contador_assincrono_m16_4_a, contador_assincrono_m16_4_b, contador_assincrono_m16_4_c,
       contador_assincrono_m16_4_d, contador_assincrono_m16_5_a, contador_assincrono_m16_5_b,
       contador_assincrono_m16_5_c, contador_assincrono_m16_5_d, contador_assincrono_m16_6_a,
       contador_assincrono_m16_6_b, contador_assincrono_m16_6_c, contador_assincrono_m16_6_d, decoder_1_a_2,
       decoder_1_b_2, decoder_1_c_2, decoder_1_d_2, decoder_1_e, decoder_1_f, decoder_1_g, decoder_2_a_2,
       decoder_2_b_2, decoder_2_c_2, decoder_2_d_2, decoder_2_e, decoder_2_f, decoder_2_g, decoder_3_a_2,
       decoder_3_b_2, decoder_3_c_2, decoder_3_d_2, decoder_3_e, decoder_3_f, decoder_3_g, decoder_4_a_2,
       decoder_4_b_2, decoder_4_c_2, decoder_4_d_2, decoder_4_e, decoder_4_f, decoder_4_g, decoder_5_a_2,
       decoder_5_b_2, decoder_5_c_2, decoder_5_d_2, decoder_5_e, decoder_5_f, decoder_5_g, decoder_6_a_2,
       decoder_6_b_2, decoder_6_c_2, decoder_6_d_2, decoder_6_e, decoder_6_f, decoder_6_g, or_1_out,
       or_2_out, or_3_out, or_4_out, or_5_out, or_6_out;

  and and_1 (and_1_out, contador_assincrono_m16_1_c, contador_assincrono_m16_2_b);
  and and_2 (and_2_out, contador_assincrono_m16_1_c, contador_assincrono_m16_1_d);
  or or_1 (or_1_out, and_1_out, RESET, and_2_out);
  and and_3 (and_3_out, contador_assincrono_m16_2_a, contador_assincrono_m16_2_c);
  contador_assincrono_m16 contador_assincrono_m16_1 (
    .CLK(and_3_out), .CLEAR(or_1_out), .D(contador_assincrono_m16_1_d), .C(contador_assincrono_m16_1_c),
    .B(contador_assincrono_m16_1_b), .A(contador_assincrono_m16_1_a));
  contador_assincrono_m16 contador_assincrono_m16_2 (
    .CLK(and_4_out), .CLEAR(or_2_out), .D(contador_assincrono_m16_2_d), .C(contador_assincrono_m16_2_c),
    .B(contador_assincrono_m16_2_b), .A(contador_assincrono_m16_2_a));
  Decoder decoder_1 (
    .A(contador_assincrono_m16_1_a), .B(contador_assincrono_m16_1_b), .C(contador_assincrono_m16_1_c),
    .D(contador_assincrono_m16_1_d), .a_2(decoder_1_a_2), .b_2(decoder_1_b_2), .c_2(decoder_1_c_2),
    .d_2(decoder_1_d_2), .e(decoder_1_e), .f(decoder_1_f), .g(decoder_1_g));
  or or_2 (or_2_out, RESET, and_1_out, and_3_out);
  and and_4 (and_4_out, contador_assincrono_m16_3_b, contador_assincrono_m16_3_c);
  Decoder decoder_2 (
    .A(contador_assincrono_m16_2_a), .B(contador_assincrono_m16_2_b), .C(contador_assincrono_m16_2_c),
    .D(contador_assincrono_m16_2_d), .a_2(decoder_2_a_2), .b_2(decoder_2_b_2), .c_2(decoder_2_c_2),
    .d_2(decoder_2_d_2), .e(decoder_2_e), .f(decoder_2_f), .g(decoder_2_g));
  _7_Segment_Display u_7_segment_display_1 (
    .g(decoder_1_g), .f(decoder_1_f), .a(decoder_1_a_2), .b(decoder_1_b_2), .e(decoder_1_e),
    .d(decoder_1_d_2), .c(decoder_1_c_2));  // open: dp
  contador_assincrono_m16 contador_assincrono_m16_3 (
    .CLK(and_5_out), .CLEAR(or_3_out), .D(contador_assincrono_m16_3_d), .C(contador_assincrono_m16_3_c),
    .B(contador_assincrono_m16_3_b), .A(contador_assincrono_m16_3_a));
  _7_Segment_Display u_7_segment_display_2 (
    .g(decoder_2_g), .f(decoder_2_f), .a(decoder_2_a_2), .b(decoder_2_b_2), .e(decoder_2_e),
    .d(decoder_2_d_2), .c(decoder_2_c_2));  // open: dp
  or or_3 (or_3_out, RESET, and_1_out, and_4_out);
  and and_5 (and_5_out, contador_assincrono_m16_4_a, contador_assincrono_m16_4_c);
  Decoder decoder_3 (
    .A(contador_assincrono_m16_3_a), .B(contador_assincrono_m16_3_b), .C(contador_assincrono_m16_3_c),
    .D(contador_assincrono_m16_3_d), .a_2(decoder_3_a_2), .b_2(decoder_3_b_2), .c_2(decoder_3_c_2),
    .d_2(decoder_3_d_2), .e(decoder_3_e), .f(decoder_3_f), .g(decoder_3_g));
  LED led_1 ();  // open: in
  LED led_2 ();  // open: in
  or or_4 (or_4_out, RESET, and_1_out, and_5_out);
  contador_assincrono_m16 contador_assincrono_m16_4 (
    .CLK(and_6_out), .CLEAR(or_4_out), .D(contador_assincrono_m16_4_d), .C(contador_assincrono_m16_4_c),
    .B(contador_assincrono_m16_4_b), .A(contador_assincrono_m16_4_a));
  and and_6 (and_6_out, contador_assincrono_m16_5_b, contador_assincrono_m16_5_c);
  Decoder decoder_4 (
    .A(contador_assincrono_m16_4_a), .B(contador_assincrono_m16_4_b), .C(contador_assincrono_m16_4_c),
    .D(contador_assincrono_m16_4_d), .a_2(decoder_4_a_2), .b_2(decoder_4_b_2), .c_2(decoder_4_c_2),
    .d_2(decoder_4_d_2), .e(decoder_4_e), .f(decoder_4_f), .g(decoder_4_g));
  _7_Segment_Display u_7_segment_display_3 (
    .g(decoder_3_g), .f(decoder_3_f), .a(decoder_3_a_2), .b(decoder_3_b_2), .e(decoder_3_e),
    .d(decoder_3_d_2), .c(decoder_3_c_2));  // open: dp
  or or_5 (or_5_out, RESET, and_1_out, and_6_out);
  contador_assincrono_m16 contador_assincrono_m16_5 (
    .CLK(and_7_out), .CLEAR(or_5_out), .D(contador_assincrono_m16_5_d), .C(contador_assincrono_m16_5_c),
    .B(contador_assincrono_m16_5_b), .A(contador_assincrono_m16_5_a));
  _7_Segment_Display u_7_segment_display_4 (
    .g(decoder_4_g), .f(decoder_4_f), .a(decoder_4_a_2), .b(decoder_4_b_2), .e(decoder_4_e),
    .d(decoder_4_d_2), .c(decoder_4_c_2));  // open: dp
  and and_7 (and_7_out, contador_assincrono_m16_6_a, contador_assincrono_m16_6_c);
  Decoder decoder_5 (
    .A(contador_assincrono_m16_5_a), .B(contador_assincrono_m16_5_b), .C(contador_assincrono_m16_5_c),
    .D(contador_assincrono_m16_5_d), .a_2(decoder_5_a_2), .b_2(decoder_5_b_2), .c_2(decoder_5_c_2),
    .d_2(decoder_5_d_2), .e(decoder_5_e), .f(decoder_5_f), .g(decoder_5_g));
  LED led_3 ();  // open: in
  LED led_4 ();  // open: in
  or or_6 (or_6_out, and_1_out, RESET, and_7_out);
  contador_assincrono_m16 contador_assincrono_m16_6 (
    .CLK(clock_1_out), .CLEAR(or_6_out), .D(contador_assincrono_m16_6_d), .C(contador_assincrono_m16_6_c),
    .B(contador_assincrono_m16_6_b), .A(contador_assincrono_m16_6_a));
  _7_Segment_Display u_7_segment_display_5 (
    .g(decoder_5_g), .f(decoder_5_f), .a(decoder_5_a_2), .b(decoder_5_b_2), .e(decoder_5_e),
    .d(decoder_5_d_2), .c(decoder_5_c_2));  // open: dp
  Decoder decoder_6 (
    .A(contador_assincrono_m16_6_a), .B(contador_assincrono_m16_6_b), .C(contador_assincrono_m16_6_c),
    .D(contador_assincrono_m16_6_d), .a_2(decoder_6_a_2), .b_2(decoder_6_b_2), .c_2(decoder_6_c_2),
    .d_2(decoder_6_d_2), .e(decoder_6_e), .f(decoder_6_f), .g(decoder_6_g));
  _7_Segment_Display u_7_segment_display_6 (
    .g(decoder_6_g), .f(decoder_6_f), .a(decoder_6_a_2), .b(decoder_6_b_2), .e(decoder_6_e),
    .d(decoder_6_d_2), .c(decoder_6_c_2));  // open: dp
  Clock clock_1 (.out(clock_1_out));
endmodule
